# Fritzing sketch 遠端餵魚 (saved by Fritzing 0.9.3b)
breadboards: 2

parts:
  Raspberry_Pi_1 = Raspberry Pi 3 [part_number=RPI-3-V1.2]
  RELAY1 = CAR RELAY [part_number=NVF4-2 package=THT]
  RELAY2 = CAR RELAY [part_number=NVF4-2 package=THT]
  R1 = Resistor [tolerance=±5% resistance=220 package=THT]
  LED1 = LED - 3mm [color="Red (633nm)" package="3 mm [THT]"]
  R2 = Resistor [tolerance=±5% resistance=220 package=THT]
  U1 = TCM8240MD [package=tcm8240md]  # not connected

nets:
  N1: Raspberry_Pi_1.3v3, R1.Pin_1
  N2: Raspberry_Pi_1.GIPO4, R1.Pin_0
  N3: Raspberry_Pi_1.GND, RELAY1.86
  N4: Raspberry_Pi_1.5V, RELAY2.86, R2.Pin_1
  N5: LED1.anode, R2.Pin_0

notes:
  PC
  步進馬達
  加熱棒
  測溫棒
  攝影機
